# Fritzing sketch fritzing (saved by Fritzing 0.9.2b)
breadboards: 1

parts:
  Componente1 = Arduino Uno (Rev3)
  S1 = H-Bridge with L298N
  M1 = DC Motor
  M2 = DC Motor
  VCC1 = 4 x AAA Battery Mount
  J1 = Basic Servo
  J2 = Basic Servo
  J3 = Basic Servo
  J4 = Basic Servo
  J5 = Basic Servo
  J6 = Basic Servo
  IR1 = TSOP312.., 314.. [package=THT]

nets:
  N1: Componente1.A3, IR1.Data
  N2: Componente1.A4/SDA, J4.pulse
  N3: Componente1.D10_PWM/SS, J2.pulse
  N4: Componente1.D11_PWM/MOSI, J1.pulse
  N5: Componente1.D13/SCK, J3.pulse
  GND: Componente1.GND, S1.GND, VCC1.-, J1.gnd, J2.gnd, J3.gnd, J4.gnd, J5.gnd, J6.gnd, IR1.GND
  N6: Componente1.D2, S1.IN4
  N7: Componente1.D3_PWM, S1.IN3
  N8: Componente1.D5_PWM, J6.pulse
  N9: Componente1.D6_PWM, S1.IN2
  N10: Componente1.D7, S1.IN1
  N11: Componente1.5V, IR1.Vs
  VCC: S1.12V, VCC1.+, J1.vcc, J2.vcc, J3.vcc, J5.vcc, J6.vcc
  N12: S1.M1-01, M2.pin_2
  N13: S1.M1-02, M2.pin_1
  N14: S1.M2-01, M1.pin_2
  N15: S1.M2-02, M1.pin_1

custom parts:
  H-Bridge with L298N: h-bridge

// code stored in the sketch: 2FotoResistencias2Leds2Motores.fzz.ino
// Autor  Samuel  Huerta  ITMA

//  asigna  los  pines del  driver  con los del arduino
int IN1 = 11;
int IN2 = 10;
int IN3 = 9;
int IN4 = 8;
//-----------------
int LED2 =2;
int LED3= 3;
int LDR0 = A0;
int LDR1 = A1;
int threshold0 = 300;//  importante  calibrar  segun  el area  a trabajar  
int threshold1 = 300;

void setup() {    //  salida de  los  pines para leds
   ///---------------------------
 pinMode(LDR0, INPUT);
 pinMode(LDR1, INPUT);
 pinMode(LED2, OUTPUT);
 pinMode(LED3, OUTPUT);
   //   salidas para el  driver
  pinMode (IN1, OUTPUT); //11
  pinMode (IN2, OUTPUT);// 10
  pinMode (IN3, OUTPUT); //9
  pinMode (IN4, OUTPUT); //8
}
void loop() {   
                  //_--------------------Izquierda
 int sensor0 = analogRead(LDR0);
  if (sensor0 >= threshold0) {
    digitalWrite(LED2, HIGH);
    digitalWrite (IN1, HIGH);   
    digitalWrite (IN2, LOW);
    delay(100);
    } else {
    digitalWrite(LED2, LOW);
    digitalWrite (IN1, LOW);
        }       
    //--------------------A1
 int sensor1 = analogRead(LDR1);
  if (sensor1 >= threshold1) {
     digitalWrite(LED3,HIGH);
    digitalWrite (IN3, HIGH);   
    digitalWrite (IN4, LOW);
    delay(100);
    } else {
    digitalWrite(LED3,LOW);
    digitalWrite (IN3, LOW);
    
        }   
 
}



























// Autor  Samuel  Huerta  ITMA
